// Logisim project OneBit.circ as structural Verilog: 8 circuits, main circuit main
module main (
  input  in_1,
  input  W,
  input  R,
  input  W_2,
  input  R_2,
  input  W_3,
  input  R_3,
  input  Address,
  input  W_4,
  input  R_4
);

  wire and_1_out, and_2_out, and_3_out, and_4_out, Bus_memory, Bus_write_data, Cell_0_memory,
       Cell_0_write_data, Cell_1_memory, Cell_1_write_data, not_1_out, or_1_out, or_2_out, X_memory,
       X_write_data, Y_memory, Y_write_data;

  or or_1 (or_1_out, Cell_1_write_data, Cell_0_write_data);
  and and_1 (and_1_out, not_1_out, W_4);
  and and_2 (and_2_out, W_4, Address);
  // Probe on Cell_0_memory
  Register4 Cell_0 (
    .Read(and_4_out), .Read_Data(or_2_out), .Write(and_1_out), .Write_Data(Cell_0_write_data),
    .Memory(Cell_0_memory));
  // Probe on Cell_1_memory
  Register4 Cell_1 (
    .Read(and_3_out), .Read_Data(or_2_out), .Write(and_2_out), .Write_Data(Cell_1_write_data),
    .Memory(Cell_1_memory));
  not not_1 (not_1_out, Address);
  and and_3 (and_3_out, Address, R_4);
  and and_4 (and_4_out, R_4, not_1_out);
  or or_2 (or_2_out, or_1_out, in_1, Bus_write_data, Y_write_data, X_write_data);
  // Probe on X_memory
  Register4 X (.Read(R), .Read_Data(or_2_out), .Write(W), .Write_Data(X_write_data), .Memory(X_memory));
  Register4 Y (.Read(R_2), .Read_Data(or_2_out), .Write(W_2), .Write_Data(Y_write_data), .Memory(Y_memory));
  // Probe on Y_memory
  Register4 Bus (.Read(R_3), .Read_Data(or_2_out), .Write(W_3), .Write_Data(Bus_write_data), .Memory(Bus_memory));
  // Probe on Bus_memory

  // Notes on the sheet:
  //   Data Bus
endmodule

module Register (
  input  In_Bus,
  input  Clock,
  input  Read,
  input  Write
);

  wire and_1_out, and_2_out, and_3_out, nand_1_out, nand_2_out, nand_3_out, nand_4_out, not_1_out, or_1_out;

  or or_1 (or_1_out, In_Bus, and_1_out);
  and and_1 (and_1_out, nand_4_out, Write);
  and and_2 (and_2_out, Clock, Read);
  and and_3 (and_3_out, Read, or_1_out);
  not not_1 (not_1_out, and_3_out);
  nand nand_1 (nand_1_out, not_1_out, and_2_out);
  nand nand_2 (nand_2_out, and_2_out, and_3_out);
  nand nand_3 (nand_3_out, nand_1_out, nand_4_out);
  nand nand_4 (nand_4_out, nand_3_out, nand_2_out);

  // Notes on the sheet:
  //   Data
endmodule

module Register2 (
  input  In_Bus,
  input  Read,
  input  Write
);

  wire and_1_out, nand_1_out, nand_2_out, nand_3_out, nand_4_out, nand_5_out, not_1_out, or_1_out;

  or or_1 (or_1_out, In_Bus, and_1_out);
  nand nand_1 (nand_1_out, Read, or_1_out);
  and and_1 (and_1_out, nand_5_out, Write);
  not not_1 (not_1_out, nand_1_out);
  nand nand_2 (nand_2_out, nand_1_out, Read);
  nand nand_3 (nand_3_out, Read, not_1_out);
  nand nand_4 (nand_4_out, nand_2_out, nand_5_out);
  nand nand_5 (nand_5_out, nand_4_out, nand_3_out);

  // Notes on the sheet:
  //   Data
endmodule

module Register3 (
  input  In_Bus,
  input  Read,
  input  Write
);

  wire nand_1_out, nand_2_out, nand_3_out, nand_4_out, nand_5_out, nand_6_out, not_1_out, not_2_out, or_1_out;

  or or_1 (or_1_out, In_Bus, not_2_out);
  nand nand_1 (nand_1_out, Read, or_1_out);
  nand nand_2 (nand_2_out, nand_6_out, Write);
  not not_1 (not_1_out, nand_1_out);
  not not_2 (not_2_out, nand_2_out);
  nand nand_3 (nand_3_out, nand_1_out, Read);
  nand nand_4 (nand_4_out, Read, not_1_out);
  nand nand_5 (nand_5_out, nand_3_out, nand_6_out);
  nand nand_6 (nand_6_out, nand_5_out, nand_4_out);

  // Notes on the sheet:
  //   Read Data
  //   Write Data
endmodule

module Register4 (
  input  Read,
  input  Read_Data,
  input  Write,
  output Memory,
  output Write_Data
);

  wire nand_1_out, nand_2_out, nand_3_out, nand_4_out, nand_5_out, not_2_out;

  nand nand_1 (nand_1_out, Read, Read_Data);
  not not_1 (Write_Data, nand_2_out);
  nand nand_2 (nand_2_out, Memory, Write);
  not not_2 (not_2_out, nand_1_out);
  nand nand_3 (nand_3_out, nand_1_out, Read);
  nand nand_4 (nand_4_out, Read, not_2_out);
  nand nand_5 (nand_5_out, nand_3_out, Memory);
  nand nand_6 (Memory, nand_5_out, nand_4_out);
endmodule

module T_Trigger (
  input  Read
);

  wire nand_1_out, nand_2_out, nand_3_out, nand_4_out, nand_5_out, nand_6_out, nand_7_out, nand_8_out,
       not_1_out;

  not not_1 (not_1_out, Read);
  nand nand_1 (nand_1_out, nand_8_out, Read);
  nand nand_2 (nand_2_out, Read, nand_7_out);
  nand nand_3 (nand_3_out, nand_1_out, nand_4_out);
  nand nand_4 (nand_4_out, nand_3_out, nand_2_out);
  nand nand_5 (nand_5_out, nand_3_out, not_1_out);
  nand nand_6 (nand_6_out, not_1_out, nand_4_out);
  nand nand_7 (nand_7_out, nand_5_out, nand_8_out);
  nand nand_8 (nand_8_out, nand_7_out, nand_6_out);
endmodule

module T_Trigger2 (
  input  in_1
);

  wire nand_1_out, nand_2_out, nand_3_out, nand_4_out, nand_5_out, nand_6_out;

  nand nand_1 (nand_1_out, in_1, nand_2_out);
  nand nand_2 (nand_2_out, nand_1_out, nand_4_out);
  nand nand_3 (nand_3_out, nand_1_out, in_1, nand_4_out);
  nand nand_4 (nand_4_out, nand_3_out, nand_6_out);
  nand nand_5 (nand_5_out, nand_1_out, nand_6_out);
  nand nand_6 (nand_6_out, nand_5_out, nand_3_out);
endmodule

module Ram (
  input  Read,
  input  Read_Data,
  input  Write,
  input  Address,
  output Cell_0,
  output Cell_1,
  output Write_Data
);

  wire Cell_0_write_data, Cell_1_write_data, nor_1_out, nor_2_out, nor_3_out, nor_4_out, not_1_out,
       not_2_out, not_3_out;

  or or_1 (Write_Data, Cell_0_write_data, Cell_1_write_data);
  not not_1 (not_1_out, Write);
  nor nor_1 (nor_1_out, not_2_out, not_1_out);
  nor nor_2 (nor_2_out, not_1_out, Address);
  Register4 u_Cell_0 (
    .Read(nor_4_out), .Read_Data(Read_Data), .Write(nor_2_out), .Write_Data(Cell_0_write_data),
    .Memory(Cell_0));
  Register4 u_Cell_1 (
    .Read(nor_3_out), .Read_Data(Read_Data), .Write(nor_1_out), .Write_Data(Cell_1_write_data),
    .Memory(Cell_1));
  not not_2 (not_2_out, Address);
  not not_3 (not_3_out, Read);
  nor nor_3 (nor_3_out, not_2_out, not_3_out);
  nor nor_4 (nor_4_out, not_3_out, Address);
endmodule
